# Fritzing sketch Signalboy (saved by Fritzing 0.9.10b)
stripboards: 1

parts:
  Part2 = Arduino Nano 33 IOT
  Part3 = LCD Keypad Shield  # not connected
  Part5 = Arduino Uno (Rev3)
  Part6 = I2C level shifter bidirectional
  Part7 = TRRS 3.5mm Jack Breakout
  Part8 = Adafruit DS3231 STEMMA QT [part_number="Adafruit #5188"]
  R1 = Resistor [tolerance=±5% power=0.25 resistance=2.2k package=THT]
  R2 = Resistor [tolerance=±5% power=0.25 resistance=1k package=THT]

nets:
  N1: Part2.RESET, Part2.A7
  GND: Part2.GND, Part2.D13~, Part5.GND, Part6.GND, Part7.SLEEVE, Part8.GND
  N2: Part2.D2, Part5.D5_PWM
  N3: Part2.D3~, Part5.D4
  N4: Part2.D4, Part5.D6_PWM
  N5: Part2.D6~, Part5.D7
  N6: Part2.D7, Part5.D8
  N7: Part2.D8, Part5.D9_PWM
  N8: Part2.D9~, Part5.D10_PWM/SS
  N9: Part2.D10~, Part6.LV4
  +5V: Part2.D11/MOSI, Part2.+5V, Part5.5V, Part6.HV
  N10: Part2.A5, Part8.SCL
  N11: Part2.A4, Part8.SDA, Part8.VBAT, Part8.32KHZ
  N12: Part2.A1, Part8.SQW
  N13: Part2.A0, R1.Pin_0
  3V3: Part2.3V3, Part6.LV, Part8.VCC
  N14: Part5.A0, R2.Pin_1
  N15: Part6.HV4, Part7.TIP
  N16: R1.Pin_1, R2.Pin_0

notes:
  BLINK

custom parts:
  Arduino Nano 33 IOT: The Arduino Nano 33 IoT is the easiest and cheapest point of entry to enhance existing devices (and creating new ones) to be part of the IoT and designing pico-network applications. Whether you are looking at building a sensor network connected to your office or home router, or if you want to create a BLE device sending data to a cellphone, the Nano 33 IoT is your one-stop-solution for many of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
  LCD Keypad Shield: It consists of a 1602 white character blue backlight LCD. The keypad consists of 5 keys — select, up, right, down and left. To save the digital IO pins, the keypad interface uses only one ADC channel. The key value is read through a 5 stage voltage divider.
  Adafruit DS3231 STEMMA QT: The datasheet for the DS3231 explains that this part is an "Extremely Accurate I²C-Integrated RTC/TCXO/Crystal". And, hey, it does exactly what it says on the tin! This Real Time Clock (RTC) is the most precise you can get in a small, low-power package. We've had a breakout board version of this RTC for a while, but we want to make it even easier for folks to use, so now it comes with STEMMA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
